// Logisim project circuito-a-avance-proyecto-arquitectura.circ as structural Verilog: 1 circuit, main circuit main
module main (
  input  A,
  input  B,
  input  C,
  input  D
);

  wire and_1_out, and_2_out, and_3_out, and_4_out, and_5_out, and_6_out, not_1_out, not_2_out, not_3_out,
       or_1_out, or_2_out;

  not not_1 (not_1_out, A);
  not not_2 (not_2_out, B);
  not not_3 (not_3_out, C);
  and and_1 (and_1_out, A, B, C);
  and and_2 (and_2_out, A, B, D);
  and and_3 (and_3_out, C, D, B);
  and and_4 (and_4_out, C, D, A);
  and and_5 (and_5_out, A, B, C, D);
  or or_1 (or_1_out, and_1_out, and_2_out, and_3_out, and_5_out, and_4_out);
  and and_6 (and_6_out, not_1_out, D, not_2_out, not_3_out);
  or or_2 (or_2_out, or_1_out, and_6_out);
  LED led_1 (.in(or_2_out));

  // Notes on the sheet:
  //   Circuito A)
  //   Alejandro Araya Jiménez
  //   Luz Valeria Villatoro Méndez
endmodule
